# Fritzing sketch arduino_ir_receiver (saved by Fritzing 0.8.3b)
breadboards: 1

parts:
  Part1 = Arduino Micro (Rev3)  # not connected
  IR1 = TSOP312.., 314.. [package=THT]
  C1 = Electrolytic Capacitor [capacitance=1μF package="0405 [SMD, electrolytic]"]
  LED1 = LED - 5mm [color="Red (633nm)" package="5 mm [THT]"]  # not connected
  LED2 = LED - 5mm [color="Green (555nm)" package="5 mm [THT]"]  # not connected
  R1 = Resistor [tolerance=±5% resistance=47 package=THT]
  IC1 = IC, DIP package, 8 pins [chip_label=IC]  # not connected
  IC2 = IC, DIP package, 8 pins [chip_label=IC]  # not connected
  R2 = PHOTOCELL [package=photocell]  # not connected

nets:
  N1: IR1.GND, C1.+, R1.Pin_0
  N2: IR1.Vs, C1.-
